# Fritzing sketch Circuit_diagram (saved by Fritzing 0.9.5d)
breadboards: 1

parts:
  Water_Level_Sensor = Water Level Sensor
  KY-016_3_color_LED_module = KY-016 RGB Full Color LED Module [package="Breakout board"]
  Componente1 = Arduino Nano (Rev3.0)
  U1 = LCD-16X2 [package=lcd-16x2_noholes]
  LCM1602_IIC1 = LCM1602 IIC [part_number="LCM1602 IIC" chip_label="LCM1602 IIC" package="DIP (Dual Inline) [THT]"]
  buz1 = Piezo Buzzer
  VCC1 = Battery
  S1 = Toggle Switch [package=THT]

nets:
  N1: Water_Level_Sensor.SIG, Componente1.A0
  VCC: Water_Level_Sensor.VCC, Componente1.5V, LCM1602_IIC1.VCC
  GND: Water_Level_Sensor.GND, KY-016_3_color_LED_module.-, Componente1.GND, LCM1602_IIC1.GND, buz1.pin_2, VCC1.-
  N2: KY-016_3_color_LED_module.R, Componente1.D2
  N3: KY-016_3_color_LED_module.G, Componente1.D3
  N4: KY-016_3_color_LED_module.B, Componente1.D4
  N5: Componente1.D9, buz1.pin_1
  N6: Componente1.VIN, S1.L2
  N7: Componente1.A5, LCM1602_IIC1.SCL
  N8: Componente1.A4, LCM1602_IIC1.SDA
  VSS: U1.VSS, LCM1602_IIC1.VSS
  VDD: U1.VDD, LCM1602_IIC1.VDD
  N9: U1.VO, LCM1602_IIC1.V0
  N10: U1.RS, LCM1602_IIC1.RS
  N11: U1.R_W, LCM1602_IIC1.RW
  N12: U1.E, LCM1602_IIC1.E
  N13: U1.DB0, LCM1602_IIC1.D0
  N14: U1.DB1, LCM1602_IIC1.D1
  N15: U1.DB2, LCM1602_IIC1.D2
  N16: U1.DB3, LCM1602_IIC1.D3
  N17: U1.DB4, LCM1602_IIC1.D4
  N18: U1.DB5, LCM1602_IIC1.D5
  N19: U1.DB6, LCM1602_IIC1.D6
  N20: U1.DB7, LCM1602_IIC1.D7
  N21: U1.A, LCM1602_IIC1.A
  N22: U1.K, LCM1602_IIC1.K
  N23: LCM1602_IIC1.LED_A, LCM1602_IIC1.LED_B
  N24: VCC1.+, S1.L1

custom parts:
  Water Level Sensor: A water level sensor. This sensor operates at 3V to 5V. The Sig (signal) pin outputs an analogue signal that is in proportion to the amount of water in contact with the sensor.
  KY-016 RGB Full Color LED Module: KY-016 Arduino full color 5mm RGB LED, different colors can be obtained by mixing the three primary colors.
  LCM1602 IIC: I2C-Module to use a 1602 or 2004 LCD on with the wire.h libory Serial LCD Modul
  Piezo Buzzer: Part from https://www.nutsvolts.com/magazine/article/november2012_SmileysWorkshop modified to be .3 in spacing to match the adafruit buzzer 5V breadboard friendly part.
  Battery: Your standard 2x 18650 battery pack (7,4 Volts)
